# Fritzing sketch MiniProjectA (saved by Fritzing 0.9.3b)
breadboards: 1

parts:
  Raspberry_Pi1 = Raspberry Pi 3 [part_number=RPI-3-V1.2]
  ADC1 = MCP3008 [package=dil16]
  U1 = POT [package=3362u]
  R1 = Photocell (LDR) [package=THT]
  U2 = MCP9700 [package=sot23-3]
  R2 = Resistor [tolerance=±5% resistance=10k package=THT]
  S1 = Pushbutton [package="[THT]"]
  S2 = Pushbutton [package="[THT]"]
  S3 = Pushbutton [package="[THT]"]
  S4 = Pushbutton [package="[THT]"]
  LED1 = smd LED [color="Red (633nm)" package="1206 [SMD]"]
  R3 = Resistor [tolerance=±5% resistance=330 package="0603 [SMD]"]
  MCP4912 = IC, DIP package, 8 pins [chip_label=MCP4911]
  C3 = Ceramic Capacitor [capacitance=10µF package="100 mil [THT, multilayer]"]
  C4 = Ceramic Capacitor [capacitance=100nF package="100 mil [THT, multilayer]"]
  MCP7940M = MCP7940M RTC
  C1 = Ceramic Capacitor [capacitance=7pF package="0603 [SMD, multilayer]"]
  C2 = Ceramic Capacitor [capacitance=7pF package="0603 [SMD, multilayer]"]
  Y1 = CRYSTAL [package=crystal-32khz-smd]

nets:
  3V3: Raspberry_Pi1.3v3, Raspberry_Pi1.3V3, ADC1.VREF, ADC1.VDD, U1.E, R1.pin_0, U2.VCC, MCP4912.pin1, MCP4912.pin6, C3.1, C4.1, MCP7940M.pin8
  N1: Raspberry_Pi1.GPIO2, MCP7940M.pin5
  N2: Raspberry_Pi1.GPIO3, MCP7940M.pin6
  GND: Raspberry_Pi1.GND, ADC1.DGND, ADC1.AGND, U1.A, U2.GND, R2.Pin_1, S1.Pin_3, S1.Pin_4, S2.Pin_3, S2.Pin_4, S3.Pin_4, S4.Pin_4, R3.Pin_0, MCP4912.pin5, MCP4912.pin7, C3.0, C4.0, MCP7940M.pin4, C1.1, C2.1
  N3: Raspberry_Pi1.GPIO17, S1.Pin_1
  N4: Raspberry_Pi1.GPIO27, S2.Pin_1
  N5: Raspberry_Pi1.GPIO22, S3.Pin_1
  N6: Raspberry_Pi1.GPIO10, ADC1.Din
  N7: Raspberry_Pi1.GPIO9, ADC1.Dout
  N8: Raspberry_Pi1.GPIO11, ADC1.CLK
  N9: Raspberry_Pi1.GPIO5, S4.Pin_1
  N10: Raspberry_Pi1.GPIO21, MCP4912.pin3
  N11: Raspberry_Pi1.GPIO20, MCP4912.pin4
  N12: Raspberry_Pi1.GPIO7, MCP4912.pin2
  N13: Raspberry_Pi1.GPIO8, ADC1.CS/SHDN
  N14: Raspberry_Pi1.GPIO18, LED1.anode
  N15: ADC1.CH0, U2.VO
  N16: ADC1.CH1, R1.pin_1, R2.Pin_0
  N17: ADC1.CH2, U1.S
  N18: LED1.cathode, R3.Pin_1
  Vout: MCP4912.pin8
  N19: MCP7940M.X1, C1.0, Y1.2
  N20: MCP7940M.X2, C2.0, Y1.1
